# Fritzing sketch seven LED wired (saved by Fritzing 0.7.9b)
breadboards: 3

parts:
  R1 = Resistor [tolerance=±5% resistance=470 package=THT]
  R2 = Resistor [tolerance=±5% resistance=470 package=THT]
  R3 = Resistor [tolerance=±5% resistance=470 package=THT]
  R4 = Resistor [tolerance=±5% resistance=470 package=THT]
  R5 = Resistor [tolerance=±5% resistance=470 package=THT]
  R6 = Resistor [tolerance=±5% resistance=470 package=THT]
  R7 = Resistor [tolerance=±5% resistance=470 package=THT]
  LED1 = LED - 5mm [color="Green (570nm)" package="5 mm [THT]"]
  LED2 = LED - 5mm [color="Green (570nm)" package="5 mm [THT]"]
  LED3 = LED - 5mm [color="Green (570nm)" package="5 mm [THT]"]
  LED4 = LED - 5mm [color="Green (570nm)" package="5 mm [THT]"]
  LED5 = LED - 5mm [color="Green (570nm)" package="5 mm [THT]"]
  LED6 = LED - 5mm [color="Green (570nm)" package="5 mm [THT]"]
  LED7 = LED - 5mm [color="Green (570nm)" package="5 mm [THT]"]
  Launchpad1 = TI Launchpad MSP430G2

nets:
  N1: R1.Pin_1, LED1.cathode
  N2: R2.Pin_1, LED2.cathode
  N3: R3.Pin_1, LED3.cathode
  N4: R4.Pin_0, Launchpad1.p20
  N5: R4.Pin_1, LED4.cathode
  N6: R5.Pin_1, LED5.cathode
  N7: R6.Pin_1, LED6.cathode
  N8: R7.Pin_1, LED7.cathode
  N9: LED1.anode, Launchpad1.p3
  N10: LED2.anode, Launchpad1.p4
  N11: LED3.anode, Launchpad1.p5
  N12: LED4.anode, Launchpad1.p6
  N13: LED5.anode, Launchpad1.p7
  N14: LED6.anode, Launchpad1.p8
  N15: LED7.anode, Launchpad1.p9
